# Fritzing sketch diagram (saved by Fritzing 0.9.9b)
breadboards: 1

parts:
  Part1 = Adafruit SCD4x [part_number="Adafruit #5187"]
  J1 = Piezo Speaker
  Mod1 = Raspberry Pi Pico

nets:
  N1: Part1.VCC, Mod1.pin_36
  N2: Part1.GND, J1.pin1, Mod1.pin_3, Mod1.pin_8, Mod1.pin_13, Mod1.pin_18, Mod1.pin_23, Mod1.pin_28, Mod1.pin_33, Mod1.pin_38, Mod1.pin_42
  N3: Part1.SCL, Mod1.pin_7
  N4: Part1.SDA, Mod1.pin_6
  N5: J1.pin2, Mod1.pin_20

custom parts:
  Adafruit SCD4x: Take a deep breath in...now slowly breathe out. Mmm isn't it wonderful? All that air around us, which we bring into our lungs, extracts oxygen from and then breathes out carbon dioxide. CO2 is essential for life on this planet we call Earth - we and plants take turns using and emitting CO2 in an elegant symbiosis. But it's important to keep that CO2 balanced - you don't want too much around,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
  Raspberry Pi Pico: Raspberry Pi Pico. Based around the RP2040 microcontroller the Pico is a low cost microcontroller device bringing Raspberry Pi quality, cost, and easy of use to the microcontroller space. Jan 2021, Split part in to two versions: tht (this one) and SMD. This one will drill holes for a .1 in header in pcb to allow plugging in the module as well as providing pads to solder the module to the top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
